# Fritzing sketch water-temperature-station (saved by Fritzing 0.9.3b)
breadboards: 1

parts:
  Part1 = Photon
  microSD1 = MicroSD Card Module
  Part2 = Adafruit Mini TFT Display - 0.96in 160x80 [part_number="Adafruit 3533"]
  Part3 = InvenSense MPU6050
  T1 = LM35 Temperature Sensor [package="TO92 [THT]"]
  DHT1 = Humidity and Temperature Sensor DHT11
  R1 = Resistor [tolerance=±20% resistance=10k package=THT]
  LED1 = LED - 5mm [color="Red (633nm)" package="5 mm [THT]"]
  S1 = Pushbutton [package="[THT]"]
  R2 = Resistor [tolerance=±5% resistance=220 package=THT]

nets:
  N1: Part1.A0, Part2.TFTRST
  N2: Part1.A1, Part2.DC
  N3: Part1.A2, Part2.SDCS
  N4: Part1.A3, microSD1.SCK
  N5: Part1.A4, microSD1.MISO, Part2.SCK
  N6: Part1.A5, microSD1.MOSI, Part2.MOSI
  N7: Part1.WKP, T1.Vout
  GND: Part1.GND, microSD1.GND, Part2.GND, Part3.GND, T1.GND, DHT1.GND_2, LED1.cathode, R2.Pin_1
  N8: Part1.D0, Part3.SDA
  N9: Part1.D1, Part3.SCL
  N10: Part1.D3, DHT1.Data-signal, R1.Pin_0
  N11: Part1.D4, microSD1.CS
  N12: Part1.D5, S1.Pin_1, S1.Pin_2, R2.Pin_0
  N13: Part1.D6, LED1.anode
  VCC: Part1.3V3, microSD1.VCC, Part2.3.3V, Part3.VCC, T1.+Vs, DHT1.Vcc, R1.Pin_1, S1.Pin_3, S1.Pin_4

notes:
  GND VCC MISO MOSI SCK CS

custom parts:
  Adafruit Mini TFT Display - 0.96in 160x80: It's the size of your thumbnail, with glorious 160x80 pixel color... it's the Adafruit Mini TFT Breakout! This very very small display is only 0.96" diagonal, packed with RGB pixels, for making very small high-density displays. The display uses 4-wire SPI to communicate and has its own pixel-addressable frame buffer, it can be used with every kind of microcontroller. Even a very small one with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
  Humidity and Temperature Sensor DHT11: Digital relative humidity & temperature sensor DHT11

// code stored in the sketch: temperatur-fritzing.ino

